# Fritzing sketch Diagrama De Conexion Arduino  (saved by Fritzing 0.9.3b)
breadboards: 1

parts:
  Componente1 = Arduino Mega 2560 (Rev3)
  J1 = Basic Servo
  Matrix_keypad2 = KEYPAD 4x4
  LCD2 = LCD screen
  LCM1602_IIC1 = generic_ic_dip_22_300mil.fzp [part_number="LCM1602 IIC" chip_label="LCM1602 IIC"]

nets:
  N1: Componente1.D21/SCL, LCM1602_IIC1.connector19
  N2: Componente1.D20/SDA, LCM1602_IIC1.connector18
  N3: Componente1.D11_PWM, J1.pulse
  5V: Componente1.5V, J1.vcc, LCM1602_IIC1.connector17
  GND: Componente1.GND, J1.gnd, LCM1602_IIC1.connector16
  N4: Componente1.D34, Matrix_keypad2.col1
  N5: Componente1.D35, Matrix_keypad2.col2
  N6: Componente1.D36, Matrix_keypad2.col3
  N7: Componente1.D37, Matrix_keypad2.col4
  N8: Componente1.D38, Matrix_keypad2.row1
  N9: Componente1.D39, Matrix_keypad2.row2
  N10: Componente1.D40, Matrix_keypad2.row3
  N11: Componente1.D41, Matrix_keypad2.row4
  N12: LCD2.VSS, LCM1602_IIC1.connector0
  N13: LCD2.VDD, LCM1602_IIC1.connector1
  N14: LCD2.V0, LCM1602_IIC1.connector2
  N15: LCD2.RS, LCM1602_IIC1.connector3
  N16: LCD2.R/W, LCM1602_IIC1.connector4
  N17: LCD2.E, LCM1602_IIC1.connector5
  N18: LCD2.DB0, LCM1602_IIC1.connector6
  N19: LCD2.DB1, LCM1602_IIC1.connector7
  N20: LCD2.DB2, LCM1602_IIC1.connector8
  N21: LCD2.DB3, LCM1602_IIC1.connector9
  N22: LCD2.DB4, LCM1602_IIC1.connector10
  N23: LCD2.DB5, LCM1602_IIC1.connector11
  N24: LCD2.DB6, LCM1602_IIC1.connector12
  N25: LCD2.DB7, LCM1602_IIC1.connector13
  N26: LCD2.LED+, LCM1602_IIC1.connector14
  N27: LCD2.LED-, LCM1602_IIC1.connector15

custom parts:
  KEYPAD 4x4: Matrix keypad 16 buttons, 4 rows x 4 columns
