# Fritzing sketch Diagrama De Conexion Raspberry Pi (saved by Fritzing 0.9.3b)
breadboards: 1

parts:
  Raspberry_Pi1 = Raspberry Pi 2
  KY-4 = Keyes Relay [package=THT]
  PIR2 = PIR sensor
  LED1 = LEDs [package=led10mm]
  Power_plug2 = Power plug
  M1 = DC Motor

nets:
  N1: Raspberry_Pi1.GPIO17, PIR2.SIG
  N2: Raspberry_Pi1.GPIO27, KY-4.ground
  GND: Raspberry_Pi1.GND, KY-4.power, PIR2.GND, LED1.C
  N3: Raspberry_Pi1.GPIO18, LED1.A
  5V: Raspberry_Pi1.5V, KY-4.signal, PIR2.VDD
  N4: KY-4.C, M1.pin_1
  N5: KY-4.NO, Power_plug2.VCC

notes:
  Este Motor Simula La Moto-Bomba Que Acciona El Flujo De Agua
  Este Simula La Corriente Alterna AC

custom parts:
  Keyes Relay: The Keyes 5V relay module is suitable for SCM development, home appliance control. It uses a 5V~12V TIL control signal which can control DC / AC signal.
